# Fritzing sketch sweepgen (saved by Fritzing 0.9.3b)
breadboards: 1

parts:
  元件1 = Arduino Nano (Rev3.0)
  S1 = Pushbutton [package="[THT]"]
  ENCODER1 = Rotary Encoder with Knob

nets:
  GND: 元件1.GND, S1.Pin_3, S1.Pin_4, ENCODER1.GND
  N1: 元件1.D2, ENCODER1.CLK
  N2: 元件1.D3, ENCODER1.DT
  N3: 元件1.D4, ENCODER1.SW
  N4: 元件1.D5, S1.Pin_1, S1.Pin_2
  N5: 元件1.5V, ENCODER1.+

custom parts:
  Rotary Encoder with Knob: Rotary Encoder with 1/4" Shaft and Knob
